# Fritzing sketch simulasi fritzinlampu lalu lintas (saved by Fritzing 0.8.7b)
breadboards: 1

parts:
  R1 = Resistor [tolerance=±20% resistance=220 package=THT]
  LED1 = LED - 5mm [color="Green (570nm)" package="5 mm [THT]"]
  R2 = Resistor [tolerance=±5% resistance=220 package=THT]
  LED2 = LED - 5mm [color="Yellow (595nm)" package="5 mm [THT]"]
  Part1 = Arduino Uno (Rev3)
  LED3 = LED - 5mm [color="Red (633nm)" package="5 mm [THT]"]
  R3 = Resistor [tolerance=±5% resistance=220 package=THT]

nets:
  N1: R1.Pin_0, LED1.anode
  N2: R1.Pin_1, R2.Pin_1, Part1.D0/RX, Part1.D1/TX
  N3: LED1.cathode, LED3.anode, R3.Pin_0
  N4: R2.Pin_0, LED2.anode
  N5: Part1.GND, LED3.cathode
  N6: Part1.D2, R3.Pin_1
